// Logisim project Labo5_Melly_Rouvinez.circ as structural Verilog: 2 circuits, main circuit COUNT_BASE
module COUNT_BASE (
  input  EN,
  input  CLK,
  input  in_3,
  output Q,
  output C
);

  wire xor_1_out;

  xor xor_1 (xor_1_out, Q, EN);
  and and_1 (C, Q, EN);
  D_Flip_Flop d_ff_1 (.D(xor_1_out), .clk(CLK), .Q(Q));  // open: Qn, preset, reset

  // Notes on the sheet:
  //   Attention, votre version de Logisim
  //   ne contient pas de tracker. Si vous
  //   enregistrez votre projet, toutes les
  //   informations du tracker seront
  //   définitivement effacées.
endmodule

module COUNT_ALL (
  input  in_1,
  output [3:0] out_2
);

  wire clock_1_out, count_base_1_c, count_base_2_c, count_base_3_c;

  Clock clock_1 (.out(clock_1_out));
  COUNT_BASE count_base_1 (.EN(in_1), .CLK(clock_1_out), .Q(out_2[0]), .C(count_base_1_c));  // open: in_3
  COUNT_BASE count_base_2 (.EN(count_base_1_c), .CLK(clock_1_out), .Q(out_2[1]), .C(count_base_2_c));  // open: in_3
  COUNT_BASE count_base_3 (.EN(count_base_2_c), .CLK(clock_1_out), .Q(out_2[2]), .C(count_base_3_c));  // open: in_3
  COUNT_BASE count_base_4 (.EN(count_base_3_c), .CLK(clock_1_out), .Q(out_2[3]));  // open: in_3, C

  // Notes on the sheet:
  //   Attention, votre version de Logisim
  //   ne contient pas de tracker. Si vous
  //   enregistrez votre projet, toutes les
  //   informations du tracker seront
  //   définitivement effacées.
endmodule
